# Fritzing sketch 1-wire-temp-sensor-DS18B20 (saved by Fritzing 0.9.4)
breadboards: 1

parts:
  Part2 = Arduino Uno (Rev3) - ICSP
  R1 = Resistor [tolerance=±5% resistance=100 package=THT]
  DS1 = DS18B20 1-Wire Temperature Sensor [part_number=DS18B20]

nets:
  N1: Part2.D12/MISO, R1.Pin_0, DS1.DQ
  5V: Part2.5V, R1.Pin_1, DS1.VDD
  GND: Part2.GND, DS1.GND
