# Fritzing sketch SG90-tower-pro-servo (saved by Fritzing 0.9.3b)

parts:
  Part1 = Arduino Uno (Rev3) - ICSP
  J1 = Basic Servo

nets:
  N1: Part1.D8, J1.pulse
  5V: Part1.5V, J1.vcc
  GND: Part1.GND, J1.gnd
